# Fritzing sketch pcb (saved by Fritzing 0.9.3b)
circuit board: 11.6747cm x 8.68906cm
circuit board: 11.6747cm x 8.68906cm
breadboards: 1

parts:
  R2 = Resistor [tolerance=±5% resistance=1k package=THT]
  R1 = Resistor [tolerance=±5% resistance=1k package=THT]
  ZS-042_RTC1 = ZS-042 RTC Module
  J3 = screw terminal, 9 pins
  J2 = female pin header, 10 pins [form="♀ (female)"]
  J1 = female pin header, 4 pins [form="♀ (female)"]
  DFRobot_DFPlayer_Mini1 = DFRobot DFPlayer Mini [part_number=DFR0299]
  J4 = screw terminal, 3 pins
  J6 = screw terminal, 2 pins
  Componente1 = Arduino Mega 2560 (Rev3)
  J5 = screw terminal, 4 pins

nets:
  N1: R2.Pin_0, Componente1.D17_PWM/RX2
  N2: R2.Pin_1, DFRobot_DFPlayer_Mini1.TX
  N3: R1.Pin_0, Componente1.D16_PWM/TX2
  N4: R1.Pin_1, DFRobot_DFPlayer_Mini1.RX
  GND: ZS-042_RTC1.GND, J3.pin9, J2.pin1, J1.pin1, DFRobot_DFPlayer_Mini1.GND-1, DFRobot_DFPlayer_Mini1.GND-2, J4.pin1, J6.pin2, Componente1.GND, J5.pin4
  VCC: ZS-042_RTC1.VCC, J2.pin10, J1.pin2, DFRobot_DFPlayer_Mini1.VCC, J6.pin1, Componente1.5V, J5.pin1
  N5: ZS-042_RTC1.SDA, J1.pin3, Componente1.D20/SDA, Componente1.SDA
  N6: ZS-042_RTC1.SCL, J1.pin4, Componente1.D21/SCL, Componente1.SCL
  N7: J3.pin1, Componente1.D23
  N8: J3.pin2, Componente1.D25
  N9: J3.pin3, Componente1.D27
  N10: J3.pin4, Componente1.D29
  N11: J3.pin5, Componente1.D31
  N12: J3.pin6, Componente1.D33
  N13: J3.pin7, Componente1.D35
  N14: J3.pin8, Componente1.D37
  N15: J2.pin2, Componente1.D36
  N16: J2.pin3, Componente1.D34
  N17: J2.pin4, Componente1.D32
  N18: J2.pin5, Componente1.D30
  N19: J2.pin6, Componente1.D28
  N20: J2.pin7, Componente1.D26
  N21: J2.pin8, Componente1.D24
  N22: J2.pin9, Componente1.D22
  N23: DFRobot_DFPlayer_Mini1.DAC_R, J4.pin3
  N24: DFRobot_DFPlayer_Mini1.DAC_L, J4.pin2
  N25: DFRobot_DFPlayer_Mini1.USB_POS, J5.pin3
  N26: DFRobot_DFPlayer_Mini1.USB_NEG, J5.pin2
